// Logisim project cart.circ as structural Verilog: 9 circuits, main circuit PIC
module PIC (
  output out_1,
  output out_2,
  output out_3,
  output out_4,
  output out_5,
  output out_6,
  output out_7,
  output out_8,
  output out_9,
  output out_10,
  output out_11,
  output out_12,
  output out_13,
  output out_14,
  output out_15,
  output out_16,
  output out_17,
  output out_18,
  output out_19,
  output out_20,
  output out_21,
  output out_22,
  output out_23,
  output out_24,
  output out_25,
  output out_26,
  output out_27,
  output out_28
);
endmodule

module Capacitor (
  output out_1,
  output out_2
);
endmodule

module Resistance (
  output out_1,
  output out_2
);
endmodule

module Switch (
  output out_1,
  output out_2
);
endmodule

module LED (
  output out_1,
  output out_2
);
endmodule

module MOS (
  output out_1,
  output out_2,
  output out_3
);
endmodule

module Relay (
  output out_1,
  output out_2,
  output out_3,
  output out_4,
  output out_5,
  output out_6,
  output out_7,
  output out_8
);
endmodule

module Motor (
  output out_1,
  output out_2
);
endmodule

module main (
  input  Vdd,
  input  Vss
);

  wire _10k_2_out_1, _10k_3_out_2, _10k_out_1, _10R_out_2, _100nF_2_out_1, _100nF_out_1, _330R_out_2,
       BK_out_1, BK_out_2, FORBAK_out_2, FT_out_1, FT_out_2, pic_1_out_5, pic_1_out_10, pic_1_out_16,
       pic_1_out_17, pic_1_out_21, POWBK_out_2, POWFT_out_2, STEER_out_2;

  Capacitor _1uF (.out_1(Vss), .out_2(Vdd));
  Resistance _330R (.out_1(Vss), .out_2(_330R_out_2));
  not LED (_330R_out_2, pic_1_out_10);
  Resistance _10k (.out_1(_10k_out_1), .out_2(Vdd));
  Switch switch_1 (.out_1(_10k_out_1), .out_2(Vss));
  Resistance _10k_2 (.out_1(_10k_2_out_1), .out_2(Vdd));
  Resistance _10k_3 (.out_1(Vdd), .out_2(_10k_3_out_2));
  PIC pic_1 (
    .out_17(pic_1_out_17), .out_12(_10k_2_out_1), .out_7(_10k_out_1), .out_8(Vdd), .out_9(Vss),
    .out_22(_10k_3_out_2), .out_21(pic_1_out_21), .out_16(pic_1_out_16), .out_3(Vss), .out_5(pic_1_out_5),
    .out_10(pic_1_out_10));  // open: out_13, out_19, out_18, out_14, out_25, out_24, out_23, out_11, out_6, out_1, out_2, out_4, out_15, out_20, out_26, out_28, out_27
  Switch switch_2 (.out_1(pic_1_out_17), .out_2(Vss));
  Resistance _10k_4 (.out_1(pic_1_out_17), .out_2(Vdd));
  Switch switch_3 (.out_1(_10k_2_out_1), .out_2(Vss));
  Resistance _10R (.out_1(Vdd), .out_2(_10R_out_2));
  Capacitor _4_7uF (.out_1(Vss), .out_2(Vdd));
  MOS POWBK (.out_1(Vss), .out_2(POWBK_out_2), .out_3(pic_1_out_10));
  Capacitor _100nF (.out_1(_100nF_out_1), .out_2(_10R_out_2));
  Resistance _100R (.out_1(_100nF_out_1), .out_2(POWBK_out_2));
  not not_1 (_10R_out_2, POWBK_out_2);
  MOS FORBAK (.out_1(Vss), .out_2(FORBAK_out_2), .out_3(pic_1_out_5));
  not not_2 (_10R_out_2, FORBAK_out_2);
  Motor BK (.out_1(BK_out_1), .out_2(BK_out_2));
  Relay relay_1 (
    .out_1(_10R_out_2), .out_2(POWBK_out_2), .out_3(BK_out_2), .out_4(POWBK_out_2), .out_5(_10R_out_2),
    .out_6(BK_out_1), .out_7(_10R_out_2), .out_8(FORBAK_out_2));
  MOS POWFT (.out_1(Vss), .out_2(POWFT_out_2), .out_3(pic_1_out_21));
  Capacitor _100nF_2 (.out_1(_100nF_2_out_1), .out_2(_10R_out_2));
  Resistance _100R_2 (.out_1(_100nF_2_out_1), .out_2(POWFT_out_2));
  not not_3 (_10R_out_2, POWFT_out_2);
  MOS STEER (.out_1(Vss), .out_2(STEER_out_2), .out_3(pic_1_out_16));
  not not_4 (_10R_out_2, STEER_out_2);
  Motor FT (.out_1(FT_out_1), .out_2(FT_out_2));
  Relay relay_2 (
    .out_1(_10R_out_2), .out_2(POWFT_out_2), .out_3(FT_out_2), .out_4(POWFT_out_2), .out_5(_10R_out_2),
    .out_6(FT_out_1), .out_7(_10R_out_2), .out_8(STEER_out_2));
  // also tied to GND on the sheet: Vss
endmodule
